# Fritzing sketch EDUSatSample01-Schematic (saved by Fritzing 1.0.5)
circuit board: 8.46667cm x 5.64444cm
stripboards: 2

parts:
  Back_Thermometer = AHT10 module
  Reaction_Wheel_-_DC_Motor = DC Motor [voltage_(max)=5V voltage_(min)=3V]
  IMU = InvenSense MPU6050
  Magnetometer = Boladge HMC5883L Compass Module
  VCC1 = Battery
  On/Off = SWITCH-SPST-2 [package=r_sw_th]
  M2 = Arduino Mega 2560+wifi R3
  Front_Thermometer = AHT10 module
  Charge_Switch = SWITCH-SPST-2 [package=r_sw_th]
  GMT130_TFT = 1_54in tft lcd
  Right_Upper_Solar_Cell = 5V 100mA Polycrystalline PET Solar Cell [part_number=IM130407002]
  Right_Lower_Solar_Cell = 5V 100mA Polycrystalline PET Solar Cell [part_number=IM130407002]
  Regulator_(5V) = LM2596 step down module
  Left_Upper_Solar_Cell = 5V 100mA Polycrystalline PET Solar Cell [part_number=IM130407002]
  Left_Lower_Solar_Cell = 5V 100mA Polycrystalline PET Solar Cell [part_number=IM130407002]
  ESP32_-_Back1 = ESP32 - CAM
  USB_Type-C_Charger = 2a2s li-ion charger [chip_label=TP4056 package="DIP (Dual Inline) [THT]"]
  L298N_-_Driver = L298N DC motor driver
  Sun_Sensor = Sun Sensor V1.0 [package="DIP (Dual Inline) [THT]"]

nets:
  N1: Back_Thermometer.Pin_1, M2.D40
  N2: Back_Thermometer.Pin_2, M2.D41
  GND: Back_Thermometer.Pin_3, IMU.GND, Magnetometer.GND, VCC1.-, M2.GND, M2.ICSP_GND, Front_Thermometer.Pin_3, GMT130_TFT.pin_1, Regulator_(5V).IN-, Regulator_(5V).OUT-, ESP32_-_Back1.GND, USB_Type-C_Charger.pin6, L298N_-_Driver.GND, Sun_Sensor.GND
  VCC: Back_Thermometer.Pin_4, IMU.VCC, Magnetometer.VCC, M2.5V, M2.ICSP_5V, Front_Thermometer.Pin_4, GMT130_TFT.pin2, ESP32_-_Back1.5V, L298N_-_Driver.5V, Sun_Sensor.Vcc
  N3: Reaction_Wheel_-_DC_Motor.pin_1, L298N_-_Driver.OUT2
  N4: Reaction_Wheel_-_DC_Motor.pin_2, L298N_-_Driver.OUT1
  N5: IMU.SCL, Magnetometer.SCL, M2.D21/SCL, M2.SCL, Front_Thermometer.Pin_1
  N6: IMU.SDA, Magnetometer.SDA, M2.D20/SDA, M2.SDA, Front_Thermometer.Pin_2
  N7: VCC1.+, On/Off.O, Charge_Switch.P
  N8: On/Off.P, Regulator_(5V).IN+
  N9: M2.A8, Left_Upper_Solar_Cell.5V
  N10: M2.A9, Left_Upper_Solar_Cell.GND
  N11: M2.A10, Left_Lower_Solar_Cell.5V
  N12: M2.A11, Left_Lower_Solar_Cell.GND
  N13: M2.A0, Right_Upper_Solar_Cell.5V
  N14: M2.A1, Right_Upper_Solar_Cell.GND
  N15: M2.A3, Right_Lower_Solar_Cell.5V
  N16: M2.A4, Right_Lower_Solar_Cell.GND
  N17: M2.D19/RX1, Sun_Sensor.TX
  N18: M2.D18/TX1, Sun_Sensor.RX
  N19: M2.D17_PWM/RX2, ESP32_-_Back1.GPIO1_/_TX
  N20: M2.D16_PWM/TX2, ESP32_-_Back1.GPIO3_/_RX
  N21: M2.D9_PWM, GMT130_TFT.pin_5
  N22: M2.D8_PWM, GMT130_TFT.pin_6
  N23: M2.D2_PWM, L298N_-_Driver.ENA
  N24: M2.D3_PWM, L298N_-_Driver.IN1
  N25: M2.D4_PWM, L298N_-_Driver.IN2
  N26: M2.D51, M2.ICSP_MOSI, GMT130_TFT.pin4
  N27: M2.D52, M2.ICSP_SCK, GMT130_TFT.pin3
  N28: Charge_Switch.O, USB_Type-C_Charger.pin3
  N29: Regulator_(5V).OUT+, L298N_-_Driver.12V

custom parts:
  AHT10 module: AHT10 Temperature Humidity Sensor Measurement Module High-Precision Digital Temp Humidity Sensor Measurement Module 1.8-6.0V I2C.
  Boladge HMC5883L Compass Module: Cheap digital compass module
  Battery: Your standard 2x 18650 battery pack (7,4 Volts)
  Arduino Mega 2560+wifi R3: Generic Arduino Mega 2560+wifi R3 board.
  1_54in tft lcd: This is the DONGKER 1.54'' LCD Display Module, SPI 240x240 1.54'' LCD Display Module ST7789 Driver 240x240 3.3V IPS LCD Display Screen Module. The 1.54" display has 240x240 color pixels.
  5V 100mA Polycrystalline PET Solar Cell: This is 5V 100mA Polycrystalline PET Solar Cell. It is high quality and exquisite appearance. It is used in all kinds of high-grade electronic products.
  LM2596 step down module: LM2596 DC-DC step down power supply module 3 A.
  ESP32 - CAM: The ESP32-CAM has a very competitive small-size camera module that can operate independently as a minimum system with a footprint of only 27*40.5*4.5mm and a deep sleep current of up to 6mA.
  2a2s li-ion charger: A DIP stand-in part for whatever IC you want. With 6 pins on a 300mil dual inline package (DIP) footprint.
  L298N DC motor driver: 2x DC motor driver with 78M05 positive voltage regulator (7..35 V) L298N: max 46 V, 2 A Set 5 V Enable jumper to enable 5 V regultor (needed for the L298N) and +5 V output at screw terminal or supply external +5 V at screw terminal Set ENA and/or ENB to +5 V to enable motor permanently or supply ENA and/or ENB with PWM signal IN1 and IN2 set rotation directory for motor A (OUT1/OUT2) IN2 and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
  Sun Sensor V1.0: A stm32 based sun sensor
